# Fritzing sketch Baseball Breadboard (saved by Fritzing 0.9.2b)
breadboards: 2

parts:
  Part1 = Arduino Uno (Rev3)
  R1 = Resistor [tolerance=±5% resistance=220 package=THT]
  R2 = Resistor [tolerance=±5% resistance=220 package=THT]
  R3 = Resistor [tolerance=±5% resistance=220 package=THT]
  R4 = Resistor [tolerance=±5% resistance=220 package=THT]
  R5 = Resistor [tolerance=±0.25% resistance=100 package=THT]
  LED1 = LED - 5mm [color="Red (633nm)" package="5 mm [THT]"]
  LED2 = LED - 5mm [color="Red (633nm)" package="5 mm [THT]"]
  LED4 = LED - 5mm [color="Yellow (585nm)" package="5 mm [THT]"]
  LED5 = LED - 5mm [color="Green (555nm)" package="5 mm [THT]"]
  S1 = Pushbutton [package="[THT]"]
  U1 = LCD-16X2 [package=lcd-16x2_noholes]
  R6 = TRIMPOT [package=3386u]
  R7 = Resistor [tolerance=±5% resistance=220 package=THT]

nets:
  N1: Part1.D8, LED4.anode
  N2: Part1.D9_PWM, LED2.anode
  N3: Part1.D10_PWM/SS, LED1.anode
  N4: Part1.D11_PWM/MOSI, U1.E
  N5: Part1.D12/MISO, U1.RS
  N6: Part1.D13/SCK, R5.Pin_1, S1.Pin_1, S1.Pin_2
  N7: Part1.D2, U1.DB7
  N8: Part1.D3_PWM, U1.DB6
  N9: Part1.D4, U1.DB5
  N10: Part1.D5_PWM, U1.DB4
  N11: Part1.D7, LED5.anode
  5V: Part1.5V, S1.Pin_3, S1.Pin_4, U1.VDD, R6.CCW, R7.Pin_1
  GND: Part1.GND, R1.Pin_0, R2.Pin_0, R3.Pin_0, R4.Pin_0, R5.Pin_0, U1.VSS, U1.R_W, U1.K, R6.CW
  N12: R1.Pin_1, LED1.cathode
  N13: R2.Pin_1, LED2.cathode
  N14: R3.Pin_1, LED4.cathode
  N15: R4.Pin_1, LED5.cathode
  N16: U1.VO, R6.WIPER
  N17: U1.A, R7.Pin_0
